// Logisim project 16_bit_CPU.circ as structural Verilog
module ALU_INT (
  input  [15:0] IN_0,
  input  [15:0] IN_1,
  input  [2:0] SEL,
  input  SET,
  input  RST,
  output [15:0] OUT_0,
  output FLAG_ZERO,
  output FLAG_POS,
  output FLAG_NEG,
  output FLAG_OVF
);

  wire adder_1_cout, adder_2_cout, bitfinder_1_found, multiplexer_2_out;
  wire [2:0] register_3_q;
  wire [15:0] adder_1_out, adder_2_out, and_1_out, multiplier_1_cout, multiplier_1_out, negator_1_out,
       not_1_out, or_1_out, register_1_q, register_2_q, shifter_1_out, xor_1_out;

  // Probe on IN_0
  // Probe on IN_1
  Register #(.width(16)) register_1 (.D(IN_0), .clk(SET), .Q(register_1_q), .clr(RST));  // open: en
  Register #(.width(16)) register_2 (.D(IN_1), .clk(SET), .Q(register_2_q), .clr(RST));  // open: en
  Register #(.width(3)) register_3 (.D(SEL), .clk(SET), .Q(register_3_q), .clr(RST));  // open: en
  Adder #(.width(16)) adder_1 (
    .a(register_1_q), .b(register_2_q), .out(adder_1_out), .cout(adder_1_cout));  // open: cin
  Negator #(.width(16)) negator_1 (.in(register_2_q), .out(negator_1_out));
  Multiplier #(.mode("twosComplement"), .width(16)) multiplier_1 (
    .a(register_1_q), .b(register_2_q), .out(multiplier_1_out), .cout(multiplier_1_cout));  // open: cin
  assign not_1_out = ~register_1_q;  // NOT_Gate not_1, 16 bits wide
  assign and_1_out = register_1_q & register_2_q;  // AND_Gate and_1, 16 bits wide
  assign or_1_out = register_1_q | register_2_q;  // OR_Gate or_1, 16 bits wide
  assign xor_1_out = register_1_q ^ register_2_q;  // XOR_Gate xor_1, 16 bits wide
  Adder #(.width(16)) adder_2 (
    .a(register_1_q), .b(negator_1_out), .out(adder_2_out), .cout(adder_2_cout));  // open: cin
  Shifter #(.shift("rl"), .width(16)) shifter_1 (.in(register_1_q), .\dist (register_2_q[3:0]), .out(shifter_1_out));
  // Probe on OUT_0
  Multiplexer #(.select(3), .width(16)) multiplexer_1 (
    .in0(adder_1_out), .in1(adder_2_out), .in2(multiplier_1_out), .in3(shifter_1_out), .in4(not_1_out),
    .in5(and_1_out), .in6(or_1_out), .in7(xor_1_out), .out(OUT_0), .sel(register_3_q));
  BitFinder #(.width(16)) bitfinder_1 (.in(multiplier_1_cout), .found(bitfinder_1_found));  // open: index
  Comparator #(.width(16)) comparator_1 (.a(OUT_0), .b({16{1'b0}}), .gt(FLAG_POS), .eq(FLAG_ZERO), .lt(FLAG_NEG));
  Multiplexer #(.select(2)) multiplexer_2 (
    .in0(adder_1_cout), .in1(adder_2_cout), .in2(bitfinder_1_found), .in3(1'b0), .out(multiplexer_2_out),
    .sel(register_3_q[1:0]));
  and and_2 (FLAG_OVF, multiplexer_2_out, ~register_3_q[2]);  // AND_Gate
endmodule

module ALU_FLT (
  input  [31:0] IN_0,
  input  [31:0] IN_1,
  input  [2:0] SEL,
  input  SET,
  input  RST,
  output [31:0] OUT_0,
  output FLAG_ZERO,
  output FLAG_POS,
  output FLAG_NEG,
  output FLAG_ERR
);

  wire fptoint_1_p2, fptoint_1_p3, fptoint_1_p4, fptoint_1_p5, fptoint_1_p6, inttofp_1_p2;
  wire [2:0] register_3_q;
  wire [15:0] fptoint_1_p7;
  wire [31:0] fpadder_1_out, fpdivider_1_out, fpmultiplier_1_out, fpsubtractor_1_out, inttofp_1_p3,
       register_1_q, register_2_q;

  Register #(.width(32)) register_1 (.D(IN_0), .clk(SET), .Q(register_1_q), .clr(RST));  // open: en
  Register #(.width(32)) register_2 (.D(IN_1), .clk(SET), .Q(register_2_q), .clr(RST));  // open: en
  Register #(.width(3)) register_3 (.D(SEL), .clk(SET), .Q(register_3_q), .clr(RST));  // open: en
  FPAdder fpadder_1 (.a(register_1_q), .b(register_2_q), .out(fpadder_1_out));
  FPSubtractor fpsubtractor_1 (.a(register_1_q), .b(register_2_q), .out(fpsubtractor_1_out));
  FPMultiplier fpmultiplier_1 (.a(register_1_q), .b(register_2_q), .out(fpmultiplier_1_out));
  FPDivider fpdivider_1 (.a(register_1_q), .b(register_2_q), .out(fpdivider_1_out));
  // FPToInt #(.mode("truncate"), .width(16)) fptoint_1: pin names not known; wires that end beside it: register_1_q, fptoint_1_p2, fptoint_1_p3, fptoint_1_p4, fptoint_1_p5, fptoint_1_p6, fptoint_1_p7
  // IntToFP #(.width(16)) inttofp_1: pin names not known; wires that end beside it: register_1_q[15:0], inttofp_1_p2, inttofp_1_p3
  Multiplexer #(.select(3), .width(32)) multiplexer_1 (
    .in0(fpadder_1_out), .in1(fpsubtractor_1_out), .in2(fpmultiplier_1_out), .in3(fpdivider_1_out),
    .in4({{16{1'b0}}, fptoint_1_p7}), .in5(inttofp_1_p3), .out(OUT_0), .sel(register_3_q));  // open: in6, in7
  Multiplexer #(.select(3)) multiplexer_2 (
    .in0(fptoint_1_p2), .in1(fptoint_1_p3), .in2(fptoint_1_p4), .in3(fptoint_1_p5), .in4(fptoint_1_p6),
    .in5(inttofp_1_p2), .out(FLAG_ERR), .sel(register_3_q));  // open: in6, in7
  // FPComparator fpcomparator_1: pin names not known; wires that end beside it: OUT_0, {32{1'b0}}, FLAG_POS, FLAG_ZERO, FLAG_NEG
endmodule

module MAIN_CTR (
  input  CLK,
  input  [15:0] JMP_ADDR,
  input  JMP_SET,
  input  RST,
  output [15:0] CTR_OUT,
  output CLK_OUT
);

  wire buffer_1_out, buffer_2_out, buffer_3_out, buffer_4_out, buffer_5_out, buffer_6_out, buffer_7_out,
       buffer_8_out, buffer_9_out, buffer_10_out, buffer_11_out;
  wire [15:0] adder_1_out, multiplexer_1_out;

  buf buffer_1 (buffer_1_out, CLK);
  buf buffer_2 (buffer_2_out, buffer_1_out);
  Multiplexer #(.width(16)) multiplexer_1 (.in0(adder_1_out), .in1(JMP_ADDR), .out(multiplexer_1_out), .sel(JMP_SET));
  Register #(.width(16)) register_1 (.D(multiplexer_1_out), .clk(buffer_2_out), .Q(CTR_OUT), .clr(RST));  // open: en
  buf buffer_3 (buffer_3_out, buffer_2_out);
  buf buffer_4 (buffer_4_out, buffer_3_out);
  buf buffer_5 (buffer_5_out, buffer_4_out);
  buf buffer_6 (buffer_6_out, buffer_5_out);
  buf buffer_7 (buffer_7_out, buffer_6_out);
  Adder #(.width(16)) adder_1 (.a(CTR_OUT), .b(16'h1), .out(adder_1_out));  // open: cin, cout
  buf buffer_8 (buffer_8_out, buffer_7_out);
  buf buffer_9 (buffer_9_out, buffer_8_out);
  buf buffer_10 (buffer_10_out, buffer_9_out);
  buf buffer_11 (buffer_11_out, buffer_10_out);
  buf buffer_12 (CLK_OUT, buffer_11_out);
endmodule

module CLK_MAIN (
  input  START,
  input  HALT,
  output CLK_OUT
);

  wire and_1_out, clock_1_out, not_1_out, or_1_out, s_r_ff_1_q;

  Clock clock_1 (.out(clock_1_out));
  or or_1 (or_1_out, START, HALT);
  LED led_1 (.in(clock_1_out));
  S_R_Flip_Flop s_r_ff_1 (.S(START), .R(HALT), .clk(or_1_out), .Q(s_r_ff_1_q));  // open: reset, Qn, preset
  and and_1 (and_1_out, s_r_ff_1_q, clock_1_out);
  not not_1 (not_1_out, and_1_out);
  and and_2 (CLK_OUT, and_1_out, not_1_out);
endmodule

module PRGM_MEM (
  input  CLK_FETCH,
  input  [15:0] JUMP_ADDR,
  input  JUMP_SET,
  input  IO_MODE,
  input  [15:0] IO_ADDR,
  input  [15:0] SET_VAL,
  input  SET_TRIG,
  input  RST,
  output [15:0] INSTRUCTION,
  output [15:0] NEXT_BYTE,
  output CLK_OUT,
  output [15:0] IO_OUT
);

  wire and_1_out, and_2_out, buffer_1_out, buffer_2_out, buffer_3_out, buffer_4_out, buffer_5_out,
       buffer_6_out, buffer_7_out, buffer_8_out, buffer_9_out, buffer_10_out, buffer_11_out, buffer_12_out,
       buffer_13_out, buffer_14_out, buffer_15_out, buffer_16_out, buffer_17_out, buffer_18_out,
       buffer_19_out, buffer_20_out, buffer_21_out, buffer_22_out, buffer_23_out, buffer_24_out,
       buffer_25_out, buffer_26_out, buffer_27_out, buffer_28_out, buffer_29_out, buffer_30_out,
       buffer_31_out, buffer_32_out, buffer_33_out, buffer_34_out, buffer_35_out, buffer_36_out,
       buffer_37_out, buffer_38_out, buffer_39_out, buffer_40_out, buffer_41_out, buffer_42_out,
       buffer_43_out, buffer_44_out, buffer_45_out, buffer_46_out, buffer_47_out, buffer_48_out,
       buffer_49_out, buffer_50_out, buffer_51_out, buffer_52_out, buffer_53_out, buffer_54_out,
       buffer_55_out, buffer_56_out, buffer_57_out, buffer_58_out, buffer_59_out, buffer_60_out,
       buffer_61_out, next_decoder_1_read_next, or_1_out, or_2_out;
  wire [15:0] demultiplexer_1_out0, demultiplexer_1_out1, main_ctr_1_ctr_out, multiplexer_1_out;

  buf buffer_1 (buffer_1_out, and_1_out);
  buf buffer_2 (buffer_2_out, buffer_1_out);
  buf buffer_3 (buffer_3_out, buffer_2_out);
  or or_1 (or_1_out, buffer_3_out, JUMP_SET, CLK_FETCH);
  or or_2 (or_2_out, buffer_3_out, CLK_FETCH, SET_TRIG);
  // Probe on main_ctr_1_ctr_out
  MAIN_CTR main_ctr_1 (
    .CLK(or_1_out), .JMP_ADDR(JUMP_ADDR), .JMP_SET(JUMP_SET), .RST(RST), .CTR_OUT(main_ctr_1_ctr_out));  // open: CLK_OUT
  buf buffer_4 (buffer_4_out, CLK_FETCH);
  buf buffer_5 (buffer_5_out, buffer_4_out);
  buf buffer_6 (buffer_6_out, buffer_5_out);
  buf buffer_7 (buffer_7_out, buffer_6_out);
  RAM #(.addrWidth(16), .dataWidth(16), .\type ("nonvolatile")) ram_1 (
    .addr(multiplexer_1_out), .we(SET_TRIG), .clk(or_2_out), .din(SET_VAL), .dout(IO_OUT));  // open: oe
  Multiplexer #(.width(16)) multiplexer_1 (
    .in0(main_ctr_1_ctr_out), .in1(IO_ADDR), .out(multiplexer_1_out), .sel(IO_MODE));
  buf buffer_8 (buffer_8_out, buffer_7_out);
  buf buffer_9 (buffer_9_out, buffer_8_out);
  buf buffer_10 (buffer_10_out, buffer_9_out);
  buf buffer_11 (buffer_11_out, buffer_10_out);
  buf buffer_12 (buffer_12_out, buffer_11_out);
  buf buffer_13 (buffer_13_out, buffer_12_out);
  buf buffer_14 (buffer_14_out, buffer_13_out);
  buf buffer_15 (buffer_15_out, buffer_14_out);
  buf buffer_16 (buffer_16_out, buffer_15_out);
  buf buffer_17 (buffer_17_out, buffer_16_out);
  buf buffer_18 (buffer_18_out, buffer_17_out);
  // Probe on IO_OUT
  buf buffer_19 (buffer_19_out, buffer_18_out);
  Demultiplexer #(.width(16)) demultiplexer_1 (
    .out0(demultiplexer_1_out0), .out1(demultiplexer_1_out1), .in(IO_OUT), .sel(buffer_22_out));
  buf buffer_20 (buffer_20_out, buffer_22_out);
  buf buffer_21 (buffer_21_out, buffer_20_out);
  buf buffer_22 (buffer_22_out, buffer_23_out);
  buf buffer_23 (buffer_23_out, buffer_24_out);
  buf buffer_24 (buffer_24_out, buffer_35_out);
  buf buffer_25 (buffer_25_out, buffer_19_out);
  buf buffer_26 (buffer_26_out, buffer_25_out);
  buf buffer_27 (buffer_27_out, buffer_26_out);
  buf buffer_28 (buffer_28_out, buffer_27_out);
  Register #(.width(16)) register_1 (
    .D(demultiplexer_1_out0), .clk(buffer_18_out), .Q(INSTRUCTION), .clr(RST));  // open: en
  Register #(.width(16)) register_2 (
    .D(demultiplexer_1_out1), .clk(buffer_29_out), .Q(NEXT_BYTE), .clr(RST));  // open: en
  buf buffer_29 (buffer_29_out, buffer_21_out);
  buf buffer_30 (buffer_30_out, buffer_28_out);
  buf buffer_31 (buffer_31_out, buffer_30_out);
  buf buffer_32 (buffer_32_out, buffer_31_out);
  buf buffer_33 (buffer_33_out, buffer_32_out);
  buf buffer_34 (buffer_34_out, buffer_35_out);
  buf buffer_35 (buffer_35_out, buffer_36_out);
  buf buffer_36 (buffer_36_out, buffer_44_out);
  buf buffer_37 (buffer_37_out, buffer_33_out);
  buf buffer_38 (buffer_38_out, buffer_37_out);
  buf buffer_39 (buffer_39_out, buffer_38_out);
  buf buffer_40 (buffer_40_out, buffer_34_out);
  buf buffer_41 (buffer_41_out, buffer_40_out);
  buf buffer_42 (buffer_42_out, buffer_41_out);
  buf buffer_43 (buffer_43_out, buffer_42_out);
  buf buffer_44 (buffer_44_out, buffer_45_out);
  buf buffer_45 (buffer_45_out, buffer_46_out);
  buf buffer_46 (buffer_46_out, buffer_47_out);
  buf buffer_47 (buffer_47_out, buffer_52_out);
  buf buffer_48 (buffer_48_out, buffer_43_out);
  buf buffer_49 (buffer_49_out, buffer_48_out);
  buf buffer_50 (buffer_50_out, buffer_49_out);
  buf buffer_51 (buffer_51_out, buffer_50_out);
  buf buffer_52 (buffer_52_out, buffer_53_out);
  buf buffer_53 (buffer_53_out, buffer_54_out);
  buf buffer_54 (buffer_54_out, buffer_55_out);
  buf buffer_55 (buffer_55_out, buffer_59_out);
  NEXT_DECODER next_decoder_1 (.INSTRUCTION(INSTRUCTION), .READ_NEXT(next_decoder_1_read_next));
  buf buffer_56 (buffer_56_out, buffer_51_out);
  buf buffer_57 (buffer_57_out, buffer_56_out);
  buf buffer_58 (buffer_58_out, buffer_57_out);
  buf buffer_59 (buffer_59_out, buffer_60_out);
  buf buffer_60 (buffer_60_out, buffer_61_out);
  buf buffer_61 (buffer_61_out, and_1_out);
  and and_1 (and_1_out, next_decoder_1_read_next, buffer_39_out);
  and and_2 (and_2_out, ~next_decoder_1_read_next, buffer_39_out);  // AND_Gate
  or or_3 (CLK_OUT, buffer_58_out, and_2_out);
endmodule

module PULSE (
  input  PLUSE_IN,
  output PULSE_OUT
);

  wire not_1_out;

  not not_1 (not_1_out, PLUSE_IN);
  and and_1 (PULSE_OUT, not_1_out, PLUSE_IN);
endmodule

module NEXT_DECODER (
  input  [15:0] INSTRUCTION,
  output READ_NEXT
);

  wire and_1_out, and_2_out, and_3_out;

  and and_1 (and_1_out, INSTRUCTION[12], ~INSTRUCTION[13], ~INSTRUCTION[14], ~INSTRUCTION[15]);  // AND_Gate
  and and_2 (and_2_out, ~INSTRUCTION[15], INSTRUCTION[14], INSTRUCTION[13]);  // AND_Gate
  and and_3 (and_3_out, INSTRUCTION[15], ~INSTRUCTION[14], INSTRUCTION[13], ~INSTRUCTION[12]);  // AND_Gate
  or or_1 (READ_NEXT, and_1_out, and_3_out, and_2_out);
endmodule

module CPU (
  input  in_1,
  input  in_2,
  input  [15:0] IN_0,
  input  [15:0] IN_1_2,
  input  [15:0] IN_2_2,
  input  [15:0] IN_3,
  output [15:0] OUT_0,
  output [15:0] OUT_1,
  output [15:0] OUT_2,
  output [15:0] OUT_3
);

  wire alu_float_section_1_alu_set, alu_float_section_1_ef_set, alu_section_1_1_alu_set,
       alu_section_1_1_reg_set_trig, alu_section_2_1_alu_set, alu_section_2_1_reg_set_trig,
       clk_main_1_clk_out, demultiplexer_2_out0, demultiplexer_2_out1, demultiplexer_2_out2,
       demultiplexer_2_out3, demultiplexer_2_out4, demultiplexer_2_out6, demultiplexer_2_out7,
       demultiplexer_2_out9, demultiplexer_2_out10, flow_section_1_halt, gp_ram_1_set_trig,
       io_section_1_set_trig, literal_jump_section_1_jump_set, load_section_1_reg_clk,
       move_section_1_set_trig, or_1_out, or_6_out, or_8_out, prgm_mem_1_clk_out;
  wire [2:0] alu_float_section_1_op_out, alu_section_1_1_alu_op_sel, alu_section_2_1_alu_op, or_7_out;
  wire [3:0] alu_flt_1_flag_zero, alu_int_1_flag_zero, alu_section_1_1_reg_sel, alu_section_1_1_reg_sel_2,
       alu_section_1_1_reg_set_sel, alu_section_2_1_reg_out_sel, alu_section_2_1_reg_sel_out,
       gp_ram_1_reg_sel, gp_ram_1_reg_sel_2, gp_ram_1_set_sel, io_section_1_read_sel, io_section_1_reg_sel,
       load_section_1_reg_sel, move_section_1_sel_out, move_section_1_sel_set, or_2_out, or_3_out, or_4_out;
  wire [11:0] demultiplexer_1_out0, demultiplexer_1_out1, demultiplexer_1_out2, demultiplexer_1_out3,
       demultiplexer_1_out4, demultiplexer_1_out6, demultiplexer_1_out7, demultiplexer_1_out9,
       demultiplexer_1_out10;
  wire [15:0] alu_int_1_out_0, alu_section_1_1_alu_in_0, alu_section_1_1_alu_in_1,
       alu_section_1_1_reg_set_val, alu_section_2_1_alu_out_0, alu_section_2_1_alu_out_1,
       alu_section_2_1_reg_out_val, gp_ram_1_set_val, io_section_1_set_val, literal_jump_section_1_jump_addr,
       load_section_1_reg_val, move_section_1_set_val, or_5_out, or_9_out, or_10_out, prgm_mem_1_instruction,
       prgm_mem_1_next_byte, registers_1_sel_2_out, registers_1_sel_out;
  wire [31:0] alu_float_section_1_ef_val, alu_flt_1_out_0, registers_1_r_ab_out, registers_1_r_cd_out;

  or or_1 (or_1_out, flow_section_1_halt, in_2);
  CLK_MAIN clk_main_1 (.START(in_1), .HALT(or_1_out), .CLK_OUT(clk_main_1_clk_out));
  PRGM_MEM prgm_mem_1 (
    .CLK_FETCH(clk_main_1_clk_out), .JUMP_ADDR(literal_jump_section_1_jump_addr),
    .JUMP_SET(literal_jump_section_1_jump_set), .RST(in_2), .INSTRUCTION(prgm_mem_1_instruction),
    .NEXT_BYTE(prgm_mem_1_next_byte), .CLK_OUT(prgm_mem_1_clk_out));  // open: IO_MODE, IO_ADDR, SET_VAL, SET_TRIG, IO_OUT
  Demultiplexer #(.select(4), .width(12)) demultiplexer_1 (
    .out0(demultiplexer_1_out0), .out1(demultiplexer_1_out1), .out2(demultiplexer_1_out2),
    .out3(demultiplexer_1_out3), .out4(demultiplexer_1_out4), .out6(demultiplexer_1_out6),
    .out7(demultiplexer_1_out7), .out9(demultiplexer_1_out9), .out10(demultiplexer_1_out10),
    .in(prgm_mem_1_instruction[11:0]), .sel(prgm_mem_1_instruction[15:12]));  // open: out5, out8, out11, out12, out13, out14, out15
  Demultiplexer #(.select(4)) demultiplexer_2 (
    .out0(demultiplexer_2_out0), .out1(demultiplexer_2_out1), .out2(demultiplexer_2_out2),
    .out3(demultiplexer_2_out3), .out4(demultiplexer_2_out4), .out6(demultiplexer_2_out6),
    .out7(demultiplexer_2_out7), .out9(demultiplexer_2_out9), .out10(demultiplexer_2_out10),
    .in(prgm_mem_1_clk_out), .sel(prgm_mem_1_instruction[15:12]));  // open: out5, out8, out11, out12, out13, out14, out15
  FLOW_SECTION flow_section_1 (.INSTR(demultiplexer_1_out0), .CLK(demultiplexer_2_out0), .HALT(flow_section_1_halt));
  LOAD_SECTION load_section_1 (
    .INSTRUCTION(demultiplexer_1_out1), .CLK(demultiplexer_2_out1), .NEXT_BYTE(prgm_mem_1_next_byte),
    .REG_SEL(load_section_1_reg_sel), .REG_CLK(load_section_1_reg_clk), .REG_VAL(load_section_1_reg_val));
  MOVE_SECTION move_section_1 (
    .INSTRUCTION(demultiplexer_1_out2), .CLK(demultiplexer_2_out2), .REG_IN(registers_1_sel_out),
    .SEL_OUT(move_section_1_sel_out), .SEL_SET(move_section_1_sel_set), .SET_VAL(move_section_1_set_val),
    .SET_TRIG(move_section_1_set_trig));
  IO_SECTION io_section_1 (
    .INSTRUTION(demultiplexer_1_out3), .CLK(demultiplexer_2_out3), .IN_0(IN_0), .IN_1(IN_1_2), .IN_2(IN_2_2),
    .IN_3(IN_3), .REG_IN(registers_1_sel_out), .RST(in_2), .REG_SEL(io_section_1_reg_sel),
    .SET_TRIG(io_section_1_set_trig), .SET_VAL(io_section_1_set_val), .READ_SEL(io_section_1_read_sel),
    .OUT_0(OUT_0), .OUT_1(OUT_1), .OUT_2(OUT_2), .OUT_3(OUT_3));
  GP_RAM gp_ram_1 (
    .INSTRUCTION(demultiplexer_1_out4), .CLK(demultiplexer_2_out4), .REG_IN(registers_1_sel_out),
    .REG_IN_2(registers_1_sel_2_out), .REG_SEL(gp_ram_1_reg_sel), .REG_SEL_2(gp_ram_1_reg_sel_2),
    .SET_SEL(gp_ram_1_set_sel), .SET_TRIG(gp_ram_1_set_trig), .SET_VAL(gp_ram_1_set_val));
  ALU_SECTION_1 alu_section_1_1 (
    .INSTRUCTION(demultiplexer_1_out6), .CLK(demultiplexer_2_out6), .NEXT_BYTE(prgm_mem_1_next_byte),
    .REG_IN(registers_1_sel_out), .REG_IN_2(registers_1_sel_2_out), .ALU_IN(alu_int_1_out_0),
    .REG_SEL(alu_section_1_1_reg_sel), .REG_SEL_2(alu_section_1_1_reg_sel_2),
    .ALU_IN_0(alu_section_1_1_alu_in_0), .ALU_IN_1(alu_section_1_1_alu_in_1),
    .ALU_OP_SEL(alu_section_1_1_alu_op_sel), .ALU_SET(alu_section_1_1_alu_set),
    .REG_SET_SEL(alu_section_1_1_reg_set_sel), .REG_SET_VAL(alu_section_1_1_reg_set_val),
    .REG_SET_TRIG(alu_section_1_1_reg_set_trig));
  ALU_SECTION_2 alu_section_2_1 (
    .INSTRUCTION(demultiplexer_1_out7), .CLK(demultiplexer_2_out7), .NEXT_BYTE(prgm_mem_1_next_byte),
    .REG_IN(registers_1_sel_out), .ALU_IN(alu_int_1_out_0), .REG_SEL_OUT(alu_section_2_1_reg_sel_out),
    .ALU_OUT_0(alu_section_2_1_alu_out_0), .ALU_OUT_1(alu_section_2_1_alu_out_1),
    .ALU_OP(alu_section_2_1_alu_op), .ALU_SET(alu_section_2_1_alu_set),
    .REG_OUT_SEL(alu_section_2_1_reg_out_sel), .REG_OUT_VAL(alu_section_2_1_reg_out_val),
    .REG_SET_TRIG(alu_section_2_1_reg_set_trig));
  ALU_FLOAT_SECTION alu_float_section_1 (
    .INSTRUCTION(demultiplexer_1_out9), .CLK(demultiplexer_2_out9), .ALU_IN(alu_flt_1_out_0),
    .OP_OUT(alu_float_section_1_op_out), .ALU_SET(alu_float_section_1_alu_set),
    .EF_VAL(alu_float_section_1_ef_val), .EF_SET(alu_float_section_1_ef_set));
  LITERAL_JUMP_SECTION literal_jump_section_1 (
    .INSTRUCTION(demultiplexer_1_out10), .CLK(demultiplexer_2_out10), .NEXT_BYTE(prgm_mem_1_next_byte),
    .CONDITIONS({alu_flt_1_flag_zero, alu_int_1_flag_zero}), .JUMP_ADDR(literal_jump_section_1_jump_addr),
    .JUMP_SET(literal_jump_section_1_jump_set));
  assign or_2_out = alu_section_1_1_reg_sel_2 | gp_ram_1_reg_sel_2;  // OR_Gate or_2, 4 bits wide
  assign or_3_out = alu_section_2_1_reg_sel_out | alu_section_1_1_reg_sel | gp_ram_1_reg_sel | io_section_1_read_sel | move_section_1_sel_out;  // OR_Gate or_3, 4 bits wide
  assign or_4_out = load_section_1_reg_sel | move_section_1_sel_set | io_section_1_reg_sel | gp_ram_1_set_sel | alu_section_1_1_reg_set_sel | alu_section_2_1_reg_out_sel;  // OR_Gate or_4, 4 bits wide
  assign or_5_out = load_section_1_reg_val | move_section_1_set_val | io_section_1_set_val | gp_ram_1_set_val | alu_section_1_1_reg_set_val | alu_section_2_1_reg_out_val;  // OR_Gate or_5, 16 bits wide
  or or_6 (or_6_out, load_section_1_reg_clk, move_section_1_set_trig, io_section_1_set_trig, gp_ram_1_set_trig, alu_section_1_1_reg_set_trig, alu_section_2_1_reg_set_trig);
  assign or_7_out = alu_section_1_1_alu_op_sel | alu_section_2_1_alu_op;  // OR_Gate or_7, 3 bits wide
  or or_8 (or_8_out, alu_section_1_1_alu_set, alu_section_2_1_alu_set);
  assign or_9_out = alu_section_1_1_alu_in_0 | alu_section_2_1_alu_out_0;  // OR_Gate or_9, 16 bits wide
  assign or_10_out = alu_section_1_1_alu_in_1 | alu_section_2_1_alu_out_1;  // OR_Gate or_10, 16 bits wide
  REGISTERS registers_1 (
    .RST(in_2), .SET_VAL(or_5_out), .SET_TRIG(or_6_out), .SET_SEL(or_4_out), .OUT_SEL(or_3_out),
    .OUT_SEL_2(or_2_out), .R_EF_VAL(alu_float_section_1_ef_val), .R_EF_SET(alu_float_section_1_ef_set),
    .R_AB_OUT(registers_1_r_ab_out), .R_CD_OUT(registers_1_r_cd_out), .SEL_OUT(registers_1_sel_out),
    .SEL_2_OUT(registers_1_sel_2_out));
  ALU_INT alu_int_1 (
    .IN_0(or_9_out), .IN_1(or_10_out), .SEL(or_7_out), .SET(or_8_out), .RST(in_2), .OUT_0(alu_int_1_out_0),
    .FLAG_ZERO(alu_int_1_flag_zero[0]), .FLAG_POS(alu_int_1_flag_zero[1]), .FLAG_NEG(alu_int_1_flag_zero[2]),
    .FLAG_OVF(alu_int_1_flag_zero[3]));
  ALU_FLT alu_flt_1 (
    .IN_0(registers_1_r_ab_out), .IN_1(registers_1_r_cd_out), .SEL(alu_float_section_1_op_out),
    .SET(alu_float_section_1_alu_set), .RST(in_2), .OUT_0(alu_flt_1_out_0),
    .FLAG_ZERO(alu_flt_1_flag_zero[0]), .FLAG_POS(alu_flt_1_flag_zero[1]), .FLAG_NEG(alu_flt_1_flag_zero[2]),
    .FLAG_ERR(alu_flt_1_flag_zero[3]));
endmodule

module REGISTERS (
  input  [3:0] OUT_SEL,
  input  [3:0] OUT_SEL_2,
  input  [3:0] SET_SEL,
  input  [15:0] SET_VAL,
  input  SET_TRIG,
  input  RST,
  input  [31:0] R_EF_VAL,
  input  R_EF_SET,
  output [15:0] SEL_OUT,
  output [15:0] SEL_2_OUT,
  output [31:0] R_AB_OUT,
  output [31:0] R_CD_OUT
);

  wire demultiplexer_1_out0, demultiplexer_1_out1, demultiplexer_1_out2, demultiplexer_1_out3,
       demultiplexer_1_out4, demultiplexer_1_out5, demultiplexer_1_out6, demultiplexer_1_out7,
       demultiplexer_1_out8, demultiplexer_1_out9, demultiplexer_1_out10, demultiplexer_1_out11,
       demultiplexer_1_out12, demultiplexer_1_out13, demultiplexer_1_out14, demultiplexer_1_out15, or_1_out,
       or_2_out;
  wire [15:0] demultiplexer_2_out0, demultiplexer_2_out1, demultiplexer_2_out2, demultiplexer_2_out3,
       demultiplexer_2_out4, demultiplexer_2_out5, demultiplexer_2_out6, demultiplexer_2_out7,
       demultiplexer_2_out8, demultiplexer_2_out9, demultiplexer_2_out10, demultiplexer_2_out11,
       demultiplexer_2_out12, demultiplexer_2_out13, demultiplexer_2_out14, demultiplexer_2_out15, or_3_out,
       or_4_out, R_0_q, R_1_q, R_2_q, R_3_q, R_4_q, R_5_q, R_6_q, R_7_q, R_8_q, R_9_q, R_E_q, R_F_q;

  Demultiplexer #(.select(4)) demultiplexer_1 (
    .out0(demultiplexer_1_out0), .out1(demultiplexer_1_out1), .out2(demultiplexer_1_out2),
    .out3(demultiplexer_1_out3), .out4(demultiplexer_1_out4), .out5(demultiplexer_1_out5),
    .out6(demultiplexer_1_out6), .out7(demultiplexer_1_out7), .out8(demultiplexer_1_out8),
    .out9(demultiplexer_1_out9), .out10(demultiplexer_1_out10), .out11(demultiplexer_1_out11),
    .out12(demultiplexer_1_out12), .out13(demultiplexer_1_out13), .out14(demultiplexer_1_out14),
    .out15(demultiplexer_1_out15), .in(SET_TRIG), .sel(SET_SEL));
  Demultiplexer #(.select(4), .width(16)) demultiplexer_2 (
    .out0(demultiplexer_2_out0), .out1(demultiplexer_2_out1), .out2(demultiplexer_2_out2),
    .out3(demultiplexer_2_out3), .out4(demultiplexer_2_out4), .out5(demultiplexer_2_out5),
    .out6(demultiplexer_2_out6), .out7(demultiplexer_2_out7), .out8(demultiplexer_2_out8),
    .out9(demultiplexer_2_out9), .out10(demultiplexer_2_out10), .out11(demultiplexer_2_out11),
    .out12(demultiplexer_2_out12), .out13(demultiplexer_2_out13), .out14(demultiplexer_2_out14),
    .out15(demultiplexer_2_out15), .in(SET_VAL), .sel(SET_SEL));
  or or_1 (or_1_out, demultiplexer_1_out14, R_EF_SET);
  or or_2 (or_2_out, demultiplexer_1_out15, R_EF_SET);
  Register #(.width(16)) R_0 (.D(demultiplexer_2_out0), .clk(demultiplexer_1_out0), .Q(R_0_q), .clr(RST));  // open: en
  Register #(.width(16)) R_1 (.D(demultiplexer_2_out1), .clk(demultiplexer_1_out1), .Q(R_1_q), .clr(RST));  // open: en
  Register #(.width(16)) R_2 (.D(demultiplexer_2_out2), .clk(demultiplexer_1_out2), .Q(R_2_q), .clr(RST));  // open: en
  Register #(.width(16)) R_3 (.D(demultiplexer_2_out3), .clk(demultiplexer_1_out3), .Q(R_3_q), .clr(RST));  // open: en
  Register #(.width(16)) R_4 (.D(demultiplexer_2_out4), .clk(demultiplexer_1_out4), .Q(R_4_q), .clr(RST));  // open: en
  Register #(.width(16)) R_5 (.D(demultiplexer_2_out5), .clk(demultiplexer_1_out5), .Q(R_5_q), .clr(RST));  // open: en
  Register #(.width(16)) R_6 (.D(demultiplexer_2_out6), .clk(demultiplexer_1_out6), .Q(R_6_q), .clr(RST));  // open: en
  Register #(.width(16)) R_7 (.D(demultiplexer_2_out7), .clk(demultiplexer_1_out7), .Q(R_7_q), .clr(RST));  // open: en
  Register #(.width(16)) R_8 (.D(demultiplexer_2_out8), .clk(demultiplexer_1_out8), .Q(R_8_q), .clr(RST));  // open: en
  Register #(.width(16)) R_9 (.D(demultiplexer_2_out9), .clk(demultiplexer_1_out9), .Q(R_9_q), .clr(RST));  // open: en
  Register #(.width(16)) R_A (
    .D(demultiplexer_2_out10), .clk(demultiplexer_1_out10), .Q(R_AB_OUT[15:0]), .clr(RST));  // open: en
  Register #(.width(16)) R_B (
    .D(demultiplexer_2_out11), .clk(demultiplexer_1_out11), .Q(R_AB_OUT[31:16]), .clr(RST));  // open: en
  Register #(.width(16)) R_C (
    .D(demultiplexer_2_out12), .clk(demultiplexer_1_out12), .Q(R_CD_OUT[15:0]), .clr(RST));  // open: en
  Register #(.width(16)) R_D (
    .D(demultiplexer_2_out13), .clk(demultiplexer_1_out13), .Q(R_CD_OUT[31:16]), .clr(RST));  // open: en
  Register #(.width(16)) R_E (.D(or_3_out), .clk(or_1_out), .Q(R_E_q), .clr(RST));  // open: en
  assign or_3_out = demultiplexer_2_out14 | R_EF_VAL[15:0];  // OR_Gate or_3, 16 bits wide
  Register #(.width(16)) R_F (.D(or_4_out), .clk(or_2_out), .Q(R_F_q), .clr(RST));  // open: en
  assign or_4_out = demultiplexer_2_out15 | R_EF_VAL[31:16];  // OR_Gate or_4, 16 bits wide
  Multiplexer #(.select(4), .width(16)) multiplexer_1 (
    .in0(R_0_q), .in1(R_1_q), .in2(R_2_q), .in3(R_3_q), .in4(R_4_q), .in5(R_5_q), .in6(R_6_q), .in7(R_7_q),
    .in8(R_8_q), .in9(R_9_q), .in10(R_AB_OUT[15:0]), .in11(R_AB_OUT[31:16]), .in12(R_CD_OUT[15:0]),
    .in13(R_CD_OUT[31:16]), .in14(R_E_q), .in15(R_F_q), .out(SEL_OUT), .sel(OUT_SEL));
  Multiplexer #(.select(4), .width(16)) multiplexer_2 (
    .in0(R_0_q), .in1(R_1_q), .in2(R_2_q), .in3(R_3_q), .in4(R_4_q), .in5(R_5_q), .in6(R_6_q), .in7(R_7_q),
    .in8(R_8_q), .in9(R_9_q), .in10(R_AB_OUT[15:0]), .in11(R_AB_OUT[31:16]), .in12(R_CD_OUT[15:0]),
    .in13(R_CD_OUT[31:16]), .in14(R_E_q), .in15(R_F_q), .out(SEL_2_OUT), .sel(OUT_SEL_2));
endmodule

module FLOW_SECTION (
  input  [11:0] INSTR,
  input  CLK,
  output HALT
);

  and and_1 (HALT, INSTR[0], CLK);
endmodule

module LOAD_SECTION (
  input  [11:0] INSTRUCTION,
  input  CLK,
  input  [15:0] NEXT_BYTE,
  output [3:0] REG_SEL,
  output REG_CLK,
  output [15:0] REG_VAL
);

  wire buffer_1_out, buffer_2_out;

  Multiplexer #(.width(4)) multiplexer_1 (.in0(4'b0000), .in1(INSTRUCTION[3:0]), .out(REG_SEL), .sel(CLK));
  Multiplexer #(.width(16)) multiplexer_2 (.in0({16{1'b0}}), .in1(NEXT_BYTE), .out(REG_VAL), .sel(CLK));
  buf buffer_1 (buffer_1_out, CLK);
  buf buffer_2 (buffer_2_out, buffer_1_out);
  buf buffer_3 (REG_CLK, buffer_2_out);
endmodule

module MOVE_SECTION (
  input  [11:0] INSTRUCTION,
  input  CLK,
  input  [15:0] REG_IN,
  output [3:0] SEL_OUT,
  output [3:0] SEL_SET,
  output [15:0] SET_VAL,
  output SET_TRIG
);

  wire buffer_1_out, buffer_2_out, buffer_3_out, buffer_4_out, buffer_5_out, buffer_6_out, buffer_7_out,
       buffer_8_out, buffer_9_out, buffer_10_out, buffer_11_out, buffer_12_out, buffer_13_out, buffer_14_out,
       buffer_15_out, buffer_16_out;

  buf buffer_1 (buffer_1_out, CLK);
  buf buffer_2 (buffer_2_out, buffer_1_out);
  buf buffer_3 (buffer_3_out, buffer_7_out);
  buf buffer_4 (buffer_4_out, buffer_3_out);
  Multiplexer #(.width(4)) multiplexer_1 (.in0(4'b0000), .in1(INSTRUCTION[7:4]), .out(SEL_OUT), .sel(buffer_5_out));
  buf buffer_5 (buffer_5_out, buffer_2_out);
  buf buffer_6 (buffer_6_out, buffer_5_out);
  buf buffer_7 (buffer_7_out, buffer_8_out);
  buf buffer_8 (buffer_8_out, buffer_9_out);
  buf buffer_9 (buffer_9_out, buffer_6_out);
  buf buffer_10 (buffer_10_out, buffer_4_out);
  buf buffer_11 (buffer_11_out, buffer_10_out);
  buf buffer_12 (buffer_12_out, buffer_11_out);
  buf buffer_13 (buffer_13_out, buffer_12_out);
  Multiplexer #(.width(4)) multiplexer_2 (.in0(4'b0000), .in1(INSTRUCTION[3:0]), .out(SEL_SET), .sel(buffer_14_out));
  Multiplexer #(.width(16)) multiplexer_3 (.in0({16{1'b0}}), .in1(REG_IN), .out(SET_VAL), .sel(buffer_14_out));
  buf buffer_14 (buffer_14_out, buffer_13_out);
  buf buffer_15 (buffer_15_out, buffer_14_out);
  buf buffer_16 (buffer_16_out, buffer_15_out);
  buf buffer_17 (SET_TRIG, buffer_16_out);
endmodule

module IO_SECTION (
  input  [11:0] INSTRUTION,
  input  CLK,
  input  [15:0] IN_0,
  input  [15:0] IN_1,
  input  [15:0] IN_2,
  input  [15:0] IN_3,
  input  [15:0] REG_IN,
  input  RST,
  output [3:0] REG_SEL,
  output SET_TRIG,
  output [15:0] SET_VAL,
  output [3:0] READ_SEL,
  output [15:0] OUT_0,
  output [15:0] OUT_1,
  output [15:0] OUT_2,
  output [15:0] OUT_3
);

  wire and_1_out, and_2_out, buffer_1_out, buffer_2_out, buffer_4_out, buffer_5_out, buffer_6_out,
       buffer_7_out, buffer_8_out, buffer_9_out, buffer_10_out, buffer_11_out, buffer_12_out, buffer_13_out,
       buffer_14_out, demultiplexer_2_out0, demultiplexer_2_out1, demultiplexer_2_out2, demultiplexer_2_out3;
  wire [15:0] demultiplexer_1_out0, demultiplexer_1_out1, demultiplexer_1_out2, demultiplexer_1_out3,
       multiplexer_1_out;

  and and_1 (and_1_out, ~INSTRUTION[10], CLK);  // AND_Gate
  and and_2 (and_2_out, INSTRUTION[10], CLK);
  Multiplexer #(.select(2), .width(16)) multiplexer_1 (
    .in0(IN_0), .in1(IN_1), .in2(IN_2), .in3(IN_3), .out(multiplexer_1_out), .sel(INSTRUTION[9:8]));
  Demultiplexer #(.select(2), .width(16)) demultiplexer_1 (
    .out0(demultiplexer_1_out0), .out1(demultiplexer_1_out1), .out2(demultiplexer_1_out2),
    .out3(demultiplexer_1_out3), .in(REG_IN), .sel(INSTRUTION[9:8]));
  Demultiplexer #(.select(2)) demultiplexer_2 (
    .out0(demultiplexer_2_out0), .out1(demultiplexer_2_out1), .out2(demultiplexer_2_out2),
    .out3(demultiplexer_2_out3), .in(buffer_14_out), .sel(INSTRUTION[9:8]));
  Multiplexer #(.width(4)) multiplexer_2 (.in0(4'b0000), .in1(INSTRUTION[3:0]), .out(REG_SEL), .sel(and_1_out));
  buf buffer_1 (buffer_1_out, and_1_out);
  buf buffer_2 (buffer_2_out, buffer_1_out);
  Multiplexer #(.width(16)) multiplexer_3 (.in0({16{1'b0}}), .in1(multiplexer_1_out), .out(SET_VAL), .sel(and_1_out));
  Multiplexer #(.width(4)) multiplexer_4 (.in0(4'b0000), .in1(INSTRUTION[3:0]), .out(READ_SEL), .sel(and_2_out));
  buf buffer_3 (SET_TRIG, buffer_2_out);
  Register #(.width(16)) register_1 (
    .D(demultiplexer_1_out0), .clk(demultiplexer_2_out0), .Q(OUT_0), .clr(RST));  // open: en
  Register #(.width(16)) register_2 (
    .D(demultiplexer_1_out1), .clk(demultiplexer_2_out1), .Q(OUT_1), .clr(RST));  // open: en
  Register #(.width(16)) register_3 (
    .D(demultiplexer_1_out2), .clk(demultiplexer_2_out2), .Q(OUT_2), .clr(RST));  // open: en
  Register #(.width(16)) register_4 (
    .D(demultiplexer_1_out3), .clk(demultiplexer_2_out3), .Q(OUT_3), .clr(RST));  // open: en
  buf buffer_4 (buffer_4_out, and_2_out);
  buf buffer_5 (buffer_5_out, buffer_4_out);
  buf buffer_6 (buffer_6_out, buffer_5_out);
  buf buffer_7 (buffer_7_out, buffer_6_out);
  buf buffer_8 (buffer_8_out, buffer_7_out);
  buf buffer_9 (buffer_9_out, buffer_8_out);
  buf buffer_10 (buffer_10_out, buffer_9_out);
  buf buffer_11 (buffer_11_out, buffer_10_out);
  buf buffer_12 (buffer_12_out, buffer_11_out);
  buf buffer_13 (buffer_13_out, buffer_12_out);
  buf buffer_14 (buffer_14_out, buffer_13_out);
endmodule

module GP_RAM (
  input  [11:0] INSTRUCTION,
  input  CLK,
  input  [15:0] REG_IN,
  input  [15:0] REG_IN_2,
  output [3:0] REG_SEL,
  output [3:0] REG_SEL_2,
  output [3:0] SET_SEL,
  output SET_TRIG,
  output [15:0] SET_VAL
);

  wire and_1_out, and_2_out, buffer_1_out, buffer_2_out, buffer_3_out, buffer_4_out, buffer_5_out,
       buffer_6_out, buffer_7_out, buffer_8_out, buffer_9_out, buffer_10_out, buffer_11_out, buffer_12_out,
       buffer_13_out, buffer_14_out, buffer_15_out, buffer_16_out, buffer_17_out, buffer_18_out,
       buffer_19_out, buffer_20_out, buffer_21_out, buffer_22_out, buffer_23_out, buffer_24_out,
       buffer_25_out, buffer_26_out, buffer_27_out, buffer_28_out, buffer_29_out, buffer_30_out,
       buffer_31_out, or_1_out, or_2_out;
  wire [15:0] ram_1_dout;

  and and_1 (and_1_out, ~INSTRUCTION[8], CLK);  // AND_Gate
  and and_2 (and_2_out, INSTRUCTION[8], CLK);
  buf buffer_1 (buffer_1_out, and_1_out);
  Multiplexer #(.width(4)) multiplexer_1 (.in0(4'b0000), .in1(INSTRUCTION[3:0]), .out(REG_SEL), .sel(and_1_out));
  Multiplexer #(.width(4)) multiplexer_2 (.in0(4'b0000), .in1(INSTRUCTION[7:4]), .out(REG_SEL_2), .sel(or_1_out));
  or or_1 (or_1_out, and_2_out, and_1_out);
  buf buffer_2 (buffer_2_out, buffer_1_out);
  buf buffer_3 (buffer_3_out, buffer_2_out);
  buf buffer_4 (buffer_4_out, buffer_3_out);
  buf buffer_5 (buffer_5_out, buffer_4_out);
  buf buffer_6 (buffer_6_out, buffer_19_out);
  or or_2 (or_2_out, buffer_19_out, buffer_21_out);
  buf buffer_7 (buffer_7_out, and_2_out);
  buf buffer_8 (buffer_8_out, buffer_7_out);
  buf buffer_9 (buffer_9_out, buffer_8_out);
  buf buffer_10 (buffer_10_out, buffer_9_out);
  buf buffer_11 (buffer_11_out, buffer_5_out);
  buf buffer_12 (buffer_12_out, buffer_11_out);
  buf buffer_13 (buffer_13_out, buffer_12_out);
  buf buffer_14 (buffer_14_out, buffer_13_out);
  RAM #(.addrWidth(16), .dataWidth(16)) ram_1 (
    .addr(REG_IN_2), .we(buffer_6_out), .clk(or_2_out), .din(REG_IN), .dout(ram_1_dout));  // open: oe
  buf buffer_15 (buffer_15_out, buffer_10_out);
  buf buffer_16 (buffer_16_out, buffer_15_out);
  buf buffer_17 (buffer_17_out, buffer_16_out);
  buf buffer_18 (buffer_18_out, buffer_17_out);
  buf buffer_19 (buffer_19_out, buffer_14_out);
  buf buffer_20 (buffer_20_out, buffer_18_out);
  buf buffer_21 (buffer_21_out, buffer_20_out);
  buf buffer_22 (buffer_22_out, buffer_21_out);
  buf buffer_23 (buffer_23_out, buffer_22_out);
  buf buffer_24 (buffer_24_out, buffer_25_out);
  buf buffer_25 (buffer_25_out, buffer_26_out);
  buf buffer_26 (buffer_26_out, buffer_29_out);
  buf buffer_27 (buffer_27_out, buffer_23_out);
  buf buffer_28 (buffer_28_out, buffer_27_out);
  buf buffer_29 (buffer_29_out, buffer_28_out);
  Multiplexer #(.width(4)) multiplexer_3 (.in0(4'b0000), .in1(INSTRUCTION[3:0]), .out(SET_SEL), .sel(buffer_24_out));
  buf buffer_30 (buffer_30_out, buffer_24_out);
  buf buffer_31 (buffer_31_out, buffer_30_out);
  buf buffer_32 (SET_TRIG, buffer_31_out);
  Multiplexer #(.width(16)) multiplexer_4 (.in0({16{1'b0}}), .in1(ram_1_dout), .out(SET_VAL), .sel(buffer_24_out));
endmodule

module ALU_SECTION_1 (
  input  [11:0] INSTRUCTION,
  input  CLK,
  input  [15:0] NEXT_BYTE,
  input  [15:0] REG_IN,
  input  [15:0] REG_IN_2,
  input  [15:0] ALU_IN,
  output [3:0] REG_SEL,
  output [3:0] REG_SEL_2,
  output [15:0] ALU_IN_0,
  output [15:0] ALU_IN_1,
  output [2:0] ALU_OP_SEL,
  output ALU_SET,
  output [3:0] REG_SET_SEL,
  output [15:0] REG_SET_VAL,
  output REG_SET_TRIG
);

  wire buffer_1_out, buffer_2_out, buffer_3_out, buffer_4_out, buffer_5_out, buffer_6_out, buffer_7_out,
       buffer_8_out, buffer_9_out, buffer_10_out, buffer_11_out, buffer_12_out, buffer_13_out, buffer_14_out,
       buffer_15_out, buffer_16_out, buffer_17_out, buffer_18_out, buffer_19_out, buffer_21_out,
       buffer_22_out, buffer_24_out, buffer_25_out, buffer_26_out, buffer_27_out, buffer_28_out,
       buffer_29_out, buffer_30_out, buffer_31_out, buffer_32_out, buffer_33_out, buffer_34_out,
       buffer_35_out, buffer_36_out, buffer_37_out, buffer_38_out, buffer_39_out, buffer_40_out,
       buffer_41_out, buffer_42_out, buffer_43_out, buffer_44_out, buffer_45_out, buffer_46_out,
       buffer_47_out, buffer_48_out, buffer_49_out, buffer_50_out, buffer_51_out;

  buf buffer_1 (buffer_1_out, CLK);
  buf buffer_2 (buffer_2_out, buffer_1_out);
  buf buffer_3 (buffer_3_out, buffer_2_out);
  buf buffer_4 (buffer_4_out, buffer_3_out);
  buf buffer_5 (buffer_5_out, buffer_4_out);
  buf buffer_6 (buffer_6_out, buffer_5_out);
  buf buffer_7 (buffer_7_out, buffer_6_out);
  buf buffer_8 (buffer_8_out, ALU_SET);
  buf buffer_9 (buffer_9_out, buffer_8_out);
  Multiplexer #(.width(4)) multiplexer_1 (.in0(4'b0000), .in1(INSTRUCTION[3:0]), .out(REG_SEL), .sel(CLK));
  Multiplexer #(.width(4)) multiplexer_2 (.in0(4'b0000), .in1(NEXT_BYTE[3:0]), .out(REG_SEL_2), .sel(CLK));
  buf buffer_10 (buffer_10_out, buffer_7_out);
  buf buffer_11 (buffer_11_out, buffer_10_out);
  buf buffer_12 (buffer_12_out, buffer_11_out);
  buf buffer_13 (buffer_13_out, buffer_12_out);
  Multiplexer #(.width(16)) multiplexer_3 (.in0({16{1'b0}}), .in1(REG_IN), .out(ALU_IN_0), .sel(buffer_13_out));
  Multiplexer #(.width(16)) multiplexer_4 (.in0({16{1'b0}}), .in1(REG_IN_2), .out(ALU_IN_1), .sel(buffer_13_out));
  Multiplexer #(.width(3)) multiplexer_5 (.in0(3'b000), .in1(INSTRUCTION[10:8]), .out(ALU_OP_SEL), .sel(buffer_13_out));
  buf buffer_14 (buffer_14_out, buffer_13_out);
  buf buffer_15 (buffer_15_out, buffer_14_out);
  buf buffer_16 (buffer_16_out, buffer_9_out);
  buf buffer_17 (buffer_17_out, buffer_16_out);
  buf buffer_18 (buffer_18_out, buffer_17_out);
  buf buffer_19 (buffer_19_out, buffer_18_out);
  buf buffer_20 (ALU_SET, buffer_15_out);
  Multiplexer #(.width(4)) multiplexer_6 (
    .in0(4'b0000), .in1(INSTRUCTION[7:4]), .out(REG_SET_SEL), .sel(buffer_40_out));
  Multiplexer #(.width(16)) multiplexer_7 (.in0({16{1'b0}}), .in1(ALU_IN), .out(REG_SET_VAL), .sel(buffer_40_out));
  buf buffer_21 (buffer_21_out, buffer_40_out);
  buf buffer_22 (buffer_22_out, buffer_21_out);
  buf buffer_23 (REG_SET_TRIG, buffer_22_out);
  buf buffer_24 (buffer_24_out, buffer_19_out);
  buf buffer_25 (buffer_25_out, buffer_24_out);
  buf buffer_26 (buffer_26_out, buffer_25_out);
  buf buffer_27 (buffer_27_out, buffer_26_out);
  buf buffer_28 (buffer_28_out, buffer_27_out);
  buf buffer_29 (buffer_29_out, buffer_28_out);
  buf buffer_30 (buffer_30_out, buffer_29_out);
  buf buffer_31 (buffer_31_out, buffer_30_out);
  buf buffer_32 (buffer_32_out, buffer_31_out);
  buf buffer_33 (buffer_33_out, buffer_32_out);
  buf buffer_34 (buffer_34_out, buffer_33_out);
  buf buffer_35 (buffer_35_out, buffer_34_out);
  buf buffer_36 (buffer_36_out, buffer_35_out);
  buf buffer_37 (buffer_37_out, buffer_36_out);
  buf buffer_38 (buffer_38_out, buffer_37_out);
  buf buffer_39 (buffer_39_out, buffer_38_out);
  buf buffer_40 (buffer_40_out, buffer_41_out);
  buf buffer_41 (buffer_41_out, buffer_42_out);
  buf buffer_42 (buffer_42_out, buffer_43_out);
  buf buffer_43 (buffer_43_out, buffer_48_out);
  buf buffer_44 (buffer_44_out, buffer_39_out);
  buf buffer_45 (buffer_45_out, buffer_44_out);
  buf buffer_46 (buffer_46_out, buffer_45_out);
  buf buffer_47 (buffer_47_out, buffer_46_out);
  buf buffer_48 (buffer_48_out, buffer_49_out);
  buf buffer_49 (buffer_49_out, buffer_51_out);
  buf buffer_50 (buffer_50_out, buffer_47_out);
  buf buffer_51 (buffer_51_out, buffer_50_out);
endmodule

module ALU_SECTION_2 (
  input  [11:0] INSTRUCTION,
  input  CLK,
  input  [15:0] NEXT_BYTE,
  input  [15:0] REG_IN,
  input  [15:0] ALU_IN,
  output [3:0] REG_SEL_OUT,
  output [15:0] ALU_OUT_0,
  output [15:0] ALU_OUT_1,
  output [2:0] ALU_OP,
  output ALU_SET,
  output [3:0] REG_OUT_SEL,
  output [15:0] REG_OUT_VAL,
  output REG_SET_TRIG
);

  wire buffer_1_out, buffer_2_out, buffer_3_out, buffer_4_out, buffer_5_out, buffer_6_out, buffer_7_out,
       buffer_8_out, buffer_9_out, buffer_10_out, buffer_11_out, buffer_12_out, buffer_13_out, buffer_14_out,
       buffer_15_out, buffer_16_out, buffer_17_out, buffer_19_out, buffer_20_out, buffer_21_out,
       buffer_22_out, buffer_23_out, buffer_24_out, buffer_26_out, buffer_27_out, buffer_28_out,
       buffer_29_out, buffer_30_out, buffer_31_out, buffer_32_out, buffer_33_out, buffer_34_out,
       buffer_35_out, buffer_36_out, buffer_37_out, buffer_38_out, buffer_39_out, buffer_40_out,
       buffer_41_out, buffer_42_out, buffer_43_out, buffer_44_out, buffer_45_out, buffer_46_out,
       buffer_47_out, buffer_48_out, buffer_49_out, buffer_50_out, buffer_51_out, buffer_52_out,
       buffer_53_out, buffer_54_out;
  wire [15:0] multiplexer_2_out, multiplexer_3_out;

  Multiplexer #(.width(4)) multiplexer_1 (.in0(4'b0000), .in1(INSTRUCTION[3:0]), .out(REG_SEL_OUT), .sel(CLK));
  buf buffer_1 (buffer_1_out, CLK);
  buf buffer_2 (buffer_2_out, buffer_1_out);
  buf buffer_3 (buffer_3_out, buffer_2_out);
  buf buffer_4 (buffer_4_out, buffer_3_out);
  buf buffer_5 (buffer_5_out, buffer_4_out);
  buf buffer_6 (buffer_6_out, buffer_5_out);
  Multiplexer #(.width(16)) multiplexer_2 (
    .in0(REG_IN), .in1(NEXT_BYTE), .out(multiplexer_2_out), .sel(INSTRUCTION[11]));
  Multiplexer #(.width(16)) multiplexer_3 (
    .in0(NEXT_BYTE), .in1(REG_IN), .out(multiplexer_3_out), .sel(INSTRUCTION[11]));
  buf buffer_7 (buffer_7_out, buffer_6_out);
  buf buffer_8 (buffer_8_out, buffer_7_out);
  buf buffer_9 (buffer_9_out, buffer_8_out);
  buf buffer_10 (buffer_10_out, buffer_9_out);
  Multiplexer #(.width(16)) multiplexer_4 (
    .in0({16{1'b0}}), .in1(multiplexer_2_out), .out(ALU_OUT_0), .sel(buffer_17_out));
  Multiplexer #(.width(16)) multiplexer_5 (
    .in0({16{1'b0}}), .in1(multiplexer_3_out), .out(ALU_OUT_1), .sel(buffer_17_out));
  Multiplexer #(.width(3)) multiplexer_6 (.in0(3'b000), .in1(INSTRUCTION[10:8]), .out(ALU_OP), .sel(buffer_17_out));
  buf buffer_11 (buffer_11_out, buffer_17_out);
  buf buffer_12 (buffer_12_out, buffer_11_out);
  buf buffer_13 (buffer_13_out, buffer_17_out);
  buf buffer_14 (buffer_14_out, buffer_13_out);
  buf buffer_15 (buffer_15_out, buffer_14_out);
  buf buffer_16 (buffer_16_out, buffer_15_out);
  buf buffer_17 (buffer_17_out, buffer_10_out);
  buf buffer_18 (ALU_SET, buffer_12_out);
  Multiplexer #(.width(4)) multiplexer_7 (
    .in0(4'b0000), .in1(INSTRUCTION[7:4]), .out(REG_OUT_SEL), .sel(buffer_34_out));
  Multiplexer #(.width(16)) multiplexer_8 (.in0({16{1'b0}}), .in1(ALU_IN), .out(REG_OUT_VAL), .sel(buffer_34_out));
  buf buffer_19 (buffer_19_out, buffer_34_out);
  buf buffer_20 (buffer_20_out, buffer_16_out);
  buf buffer_21 (buffer_21_out, buffer_20_out);
  buf buffer_22 (buffer_22_out, buffer_21_out);
  buf buffer_23 (buffer_23_out, buffer_22_out);
  buf buffer_24 (buffer_24_out, buffer_19_out);
  buf buffer_25 (REG_SET_TRIG, buffer_24_out);
  buf buffer_26 (buffer_26_out, buffer_23_out);
  buf buffer_27 (buffer_27_out, buffer_26_out);
  buf buffer_28 (buffer_28_out, buffer_27_out);
  buf buffer_29 (buffer_29_out, buffer_28_out);
  buf buffer_30 (buffer_30_out, buffer_29_out);
  buf buffer_31 (buffer_31_out, buffer_30_out);
  buf buffer_32 (buffer_32_out, buffer_31_out);
  buf buffer_33 (buffer_33_out, buffer_32_out);
  buf buffer_34 (buffer_34_out, buffer_39_out);
  buf buffer_35 (buffer_35_out, buffer_33_out);
  buf buffer_36 (buffer_36_out, buffer_35_out);
  buf buffer_37 (buffer_37_out, buffer_36_out);
  buf buffer_38 (buffer_38_out, buffer_37_out);
  buf buffer_39 (buffer_39_out, buffer_40_out);
  buf buffer_40 (buffer_40_out, buffer_41_out);
  buf buffer_41 (buffer_41_out, buffer_42_out);
  buf buffer_42 (buffer_42_out, buffer_49_out);
  buf buffer_43 (buffer_43_out, buffer_38_out);
  buf buffer_44 (buffer_44_out, buffer_43_out);
  buf buffer_45 (buffer_45_out, buffer_44_out);
  buf buffer_46 (buffer_46_out, buffer_45_out);
  buf buffer_47 (buffer_47_out, buffer_48_out);
  buf buffer_48 (buffer_48_out, buffer_52_out);
  buf buffer_49 (buffer_49_out, buffer_50_out);
  buf buffer_50 (buffer_50_out, buffer_47_out);
  buf buffer_51 (buffer_51_out, buffer_54_out);
  buf buffer_52 (buffer_52_out, buffer_51_out);
  buf buffer_53 (buffer_53_out, buffer_46_out);
  buf buffer_54 (buffer_54_out, buffer_53_out);
endmodule

module ALU_FLOAT_SECTION (
  input  [11:0] INSTRUCTION,
  input  CLK,
  input  [31:0] ALU_IN,
  output [2:0] OP_OUT,
  output ALU_SET,
  output [31:0] EF_VAL,
  output EF_SET
);

  wire buffer_1_out, buffer_2_out, buffer_3_out, buffer_4_out, buffer_5_out, buffer_6_out, buffer_7_out,
       buffer_8_out, buffer_10_out, buffer_11_out, buffer_12_out, buffer_13_out, buffer_14_out,
       buffer_15_out, buffer_16_out, buffer_17_out, buffer_18_out, buffer_19_out, buffer_20_out,
       buffer_21_out, buffer_22_out, buffer_23_out, buffer_24_out, buffer_25_out, buffer_26_out,
       buffer_27_out, buffer_28_out, buffer_29_out, buffer_30_out, buffer_31_out, buffer_32_out,
       buffer_33_out, buffer_34_out, buffer_35_out, buffer_36_out, buffer_37_out, buffer_38_out,
       buffer_39_out, buffer_40_out, buffer_41_out, buffer_42_out, buffer_43_out, buffer_44_out,
       buffer_45_out, buffer_46_out, buffer_47_out, buffer_48_out, buffer_49_out, buffer_50_out,
       buffer_51_out, buffer_52_out, buffer_53_out;

  buf buffer_1 (buffer_1_out, CLK);
  buf buffer_2 (buffer_2_out, buffer_1_out);
  buf buffer_3 (buffer_3_out, buffer_2_out);
  buf buffer_4 (buffer_4_out, buffer_3_out);
  buf buffer_5 (buffer_5_out, buffer_4_out);
  buf buffer_6 (buffer_6_out, buffer_5_out);
  Multiplexer #(.width(32)) multiplexer_1 (.in0({32{1'b0}}), .in1(ALU_IN), .out(EF_VAL), .sel(buffer_22_out));
  buf buffer_7 (buffer_7_out, buffer_22_out);
  buf buffer_8 (buffer_8_out, buffer_7_out);
  buf buffer_9 (EF_SET, buffer_8_out);
  buf buffer_10 (buffer_10_out, buffer_6_out);
  buf buffer_11 (buffer_11_out, buffer_10_out);
  buf buffer_12 (buffer_12_out, buffer_11_out);
  buf buffer_13 (buffer_13_out, buffer_12_out);
  buf buffer_14 (buffer_14_out, buffer_13_out);
  buf buffer_15 (buffer_15_out, buffer_14_out);
  buf buffer_16 (buffer_16_out, buffer_15_out);
  buf buffer_17 (buffer_17_out, buffer_16_out);
  buf buffer_18 (buffer_18_out, buffer_17_out);
  buf buffer_19 (buffer_19_out, buffer_18_out);
  buf buffer_20 (buffer_20_out, buffer_19_out);
  buf buffer_21 (buffer_21_out, buffer_20_out);
  buf buffer_22 (buffer_22_out, buffer_23_out);
  buf buffer_23 (buffer_23_out, buffer_28_out);
  buf buffer_24 (buffer_24_out, buffer_21_out);
  buf buffer_25 (buffer_25_out, buffer_24_out);
  buf buffer_26 (buffer_26_out, buffer_25_out);
  buf buffer_27 (buffer_27_out, buffer_26_out);
  buf buffer_28 (buffer_28_out, buffer_29_out);
  buf buffer_29 (buffer_29_out, buffer_30_out);
  buf buffer_30 (buffer_30_out, buffer_31_out);
  buf buffer_31 (buffer_31_out, buffer_38_out);
  buf buffer_32 (buffer_32_out, buffer_27_out);
  buf buffer_33 (buffer_33_out, buffer_32_out);
  buf buffer_34 (buffer_34_out, buffer_33_out);
  buf buffer_35 (buffer_35_out, buffer_34_out);
  buf buffer_36 (buffer_36_out, buffer_37_out);
  buf buffer_37 (buffer_37_out, buffer_44_out);
  buf buffer_38 (buffer_38_out, buffer_39_out);
  buf buffer_39 (buffer_39_out, buffer_36_out);
  buf buffer_40 (buffer_40_out, buffer_43_out);
  buf buffer_41 (buffer_41_out, buffer_40_out);
  buf buffer_42 (buffer_42_out, buffer_35_out);
  buf buffer_43 (buffer_43_out, buffer_42_out);
  buf buffer_44 (buffer_44_out, buffer_45_out);
  buf buffer_45 (buffer_45_out, buffer_46_out);
  buf buffer_46 (buffer_46_out, buffer_47_out);
  buf buffer_47 (buffer_47_out, buffer_53_out);
  buf buffer_48 (buffer_48_out, buffer_41_out);
  buf buffer_49 (buffer_49_out, buffer_48_out);
  buf buffer_50 (buffer_50_out, buffer_49_out);
  buf buffer_51 (buffer_51_out, buffer_50_out);
  buf buffer_52 (buffer_52_out, buffer_51_out);
  buf buffer_53 (buffer_53_out, buffer_52_out);

  assign ALU_SET = CLK;
  assign OP_OUT = INSTRUCTION[10:8];
endmodule

module LITERAL_JUMP_SECTION (
  input  [11:0] INSTRUCTION,
  input  CLK,
  input  [15:0] NEXT_BYTE,
  input  [7:0] CONDITIONS,
  output [15:0] JUMP_ADDR,
  output JUMP_SET
);

  wire and_1_out, and_2_out, multiplexer_1_out;

  and and_1 (and_1_out, ~INSTRUCTION[8], CLK);  // AND_Gate
  Multiplexer #(.select(3)) multiplexer_1 (
    .in0(CONDITIONS[0]), .in1(CONDITIONS[1]), .in2(CONDITIONS[2]), .in3(CONDITIONS[3]), .in4(CONDITIONS[4]),
    .in5(CONDITIONS[5]), .in6(CONDITIONS[6]), .in7(CONDITIONS[7]), .out(multiplexer_1_out),
    .sel(INSTRUCTION[6:4]));
  and and_2 (and_2_out, INSTRUCTION[8], CLK, multiplexer_1_out);
  or or_1 (JUMP_SET, and_1_out, and_2_out);

  assign JUMP_ADDR = NEXT_BYTE;
endmodule
